# Fritzing sketch newopixelwifi (saved by Fritzing 0.9.3b)
breadboards: 1

parts:
  LED2 = smd LED [color="Green (555nm)" package="1206 [SMD]"]
  R1 = Resistor [tolerance=±5% resistance=220 package="2010 [SMD]"]
  U1 = ESP32S-HiLetgo [part_number=ESP32S-HiLetgo]
  Part1 = LED Matrix - Serial Interface - Red/Green/Blue  # not connected
  5v = Power Jack [package=power_jack_smd]  # not connected

nets:
  N1: LED2.cathode, U1.GND
  N2: LED2.anode, R1.Pin_1
  N3: R1.Pin_0, U1.GPIO2

notes:
  Assume this is a 16x16 NeoPixel RGB LED Matrix. With 3 pins:
  - 5V Power
  - Data
  This type of board will convert 5v to 3.3V

custom parts:
  ESP32S-HiLetgo: HiLetgo ESP-WROOM-32 ESP32 ESP-32S Development Board 2.4GHz Dual-Mode WiFi + Bluetooth Dual Cores Microcontroller The ESP32 integrated with Antenna switches, RF Balun, power amplifiers, low-noise amplifiers, filters, and management modules, and the entire solution occupies the least area of PCB. 2.4 GHz Wi-Fi plus Bluetooth dual-mode chip, with TSMC Ultra-low power consumption 40nm technology,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
